// Logisim project CPU.circ as structural Verilog: 8 circuits, main circuit COMPUTER
module COMPUTER (
);

  wire BTN_INTR0_out, BTN_INTR1_out, BTN_INTR2_out, BTN_INTR3_out, BTN_INTR4_out, BTN_INTR5_out,
       BTN_INTR6_out, BTN_INTR7_out, BTN_RST_out, CLK, cpu_1_inta, pull_resistor_2_node,
       pull_resistor_6_node, ram_1_out_8, rst;
  wire [2:0] cpu_1_uext2__0;
  wire [7:0] interrupt_interface_8_1_intr7__0, pull_resistor_3_node, ram_1_out_7;
  wire [15:0] pull_resistor_4_node;

  Button BTN_RST (.out(BTN_RST_out));
  Clock u_CLK (.out(CLK));
  RisingEdge risingedge_1 (.INPUT(BTN_RST_out), .CLK(CLK), .OUTPUT(rst));
  RAM ram_1 (
    .in_1(pull_resistor_4_node), .in_2(CLK), .in_3(pull_resistor_3_node), .in_4(pull_resistor_2_node),
    .in_5(pull_resistor_6_node), .in_6(rst), .out_7(ram_1_out_7), .out_8(ram_1_out_8));
  Pull_Resistor pull_resistor_1 (.node(ram_1_out_7));
  Pull_Resistor pull_resistor_2 (.node(pull_resistor_2_node));
  Pull_Resistor pull_resistor_3 (.node(pull_resistor_3_node));
  Pull_Resistor pull_resistor_4 (.node(pull_resistor_4_node));
  Pull_Resistor pull_resistor_5 (.node(ram_1_out_8));
  Pull_Resistor pull_resistor_6 (.node(pull_resistor_6_node));
  CPU cpu_1 (
    .in_1(rst), .in_2(CLK), .in_3(ram_1_out_8), .in_4(ram_1_out_7), .ABUS(pull_resistor_4_node),
    .DOUTBUS(pull_resistor_3_node), .out_8(pull_resistor_2_node), .out_9(pull_resistor_6_node),
    .inta(cpu_1_inta), .intr7__0(interrupt_interface_8_1_intr7__0), .UEXT2__0(cpu_1_uext2__0));
  INTERRUPT_INTERFACE_8 interrupt_interface_8_1 (
    .BTN_INTR0(BTN_INTR0_out), .BTN_INTR1(BTN_INTR1_out), .BTN_INTR2(BTN_INTR2_out),
    .BTN_INTR3(BTN_INTR3_out), .BTN_INTR4(BTN_INTR4_out), .BTN_INTR5(BTN_INTR5_out),
    .BTN_INTR6(BTN_INTR6_out), .BTN_INTR7(BTN_INTR7_out), .inta(cpu_1_inta), .UEXT2__0(cpu_1_uext2__0),
    .CLK(CLK), .intr7__0(interrupt_interface_8_1_intr7__0));
  Button BTN_INTR7 (.out(BTN_INTR7_out));
  Button BTN_INTR6 (.out(BTN_INTR6_out));
  Button BTN_INTR5 (.out(BTN_INTR5_out));
  Button BTN_INTR4 (.out(BTN_INTR4_out));
  Button BTN_INTR3 (.out(BTN_INTR3_out));
  Button BTN_INTR2 (.out(BTN_INTR2_out));
  Button BTN_INTR1 (.out(BTN_INTR1_out));
  Button BTN_INTR0 (.out(BTN_INTR0_out));
endmodule

module CPU (
  input  in_1,
  input  in_2,
  input  in_3,
  input  [7:0] in_4,
  input  [7:0] intr7__0,
  output [15:0] ABUS,
  output [7:0] DOUTBUS,
  output out_8,
  output out_9,
  output inta,
  output [2:0] UEXT2__0
);

  wire ALUC;
  wire [3:0] common_1_phaseffbus;
  wire [6:0] common_1_addrbus, pull_resistor_2_node;
  wire [7:0] pull_resistor_7_node;
  wire [11:0] pull_resistor_4_node;
  wire [14:0] pull_resistor_5_node;
  wire [15:0] A, ALU, B, INTRADDR, PSW;
  wire [20:0] common_1_instrucbus;

  COMMON common_1 (
    .CLK(in_2), .RST(in_1), .DIN(in_4), .CMEMBUS(pull_resistor_5_node), .MAR(ABUS), .MDR(DOUTBUS),
    .PHASEFFBUS(common_1_phaseffbus), .INSTRUCBUS(common_1_instrucbus), .ADDRBUS(common_1_addrbus),
    .PSW(PSW), .CREGBUS(pull_resistor_4_node), .CFFBUS(pull_resistor_7_node), .B(B), .A(A),
    .CPSW(pull_resistor_2_node), .ALU(ALU), .IVTPPDSP(INTRADDR), .ALUC(ALUC));
  Pull_Resistor pull_resistor_1 (.node(common_1_instrucbus));
  Pull_Resistor pull_resistor_2 (.node(pull_resistor_2_node));
  Pull_Resistor pull_resistor_3 (.node(common_1_phaseffbus));
  Pull_Resistor pull_resistor_4 (.node(pull_resistor_4_node));
  Pull_Resistor pull_resistor_5 (.node(pull_resistor_5_node));
  Pull_Resistor pull_resistor_6 (.node(common_1_addrbus));
  Pull_Resistor pull_resistor_7 (.node(pull_resistor_7_node));
  FETCH fetch_1 (
    .in_1(in_1), .in_2(in_2), .in_3(in_3), .PHASEFFBUS(common_1_phaseffbus), .PSW(PSW), .rdMEM(out_9),
    .CMEMBUS(pull_resistor_5_node), .CFFBUS(pull_resistor_7_node), .CREGBUS(pull_resistor_4_node),
    .INSTRUCBUS(common_1_instrucbus), .ADDRBUS(common_1_addrbus));
  ADDR addr_1 (
    .in_1(in_1), .in_2(in_2), .in_3(in_3), .PHASEFFBUS(common_1_phaseffbus), .rdMEM(out_9),
    .CMEMBUS(pull_resistor_5_node), .CFFBUS(pull_resistor_7_node), .CREGBUS(pull_resistor_4_node),
    .INSTRUCBUS(common_1_instrucbus), .ADDRBUS(common_1_addrbus));
  EXEC exec_1 (
    .in_1(in_1), .in_2(in_2), .in_3(in_3), .B(B), .PHASEFFBUS(common_1_phaseffbus), .PSW(PSW), .A(A),
    .ALU(ALU), .CMEMBUS(pull_resistor_5_node), .CFFBUS(pull_resistor_7_node), .CREGBUS(pull_resistor_4_node),
    .CPSW(pull_resistor_2_node), .rdMEM(out_9), .wrMEM(out_8), .INSTRUCBUS(common_1_instrucbus),
    .ADDRBUS(common_1_addrbus), .ALUC(ALUC));
  INTR intr_1 (
    .in_1(in_1), .in_2(in_2), .in_3(in_3), .PHASEFFBUS(common_1_phaseffbus), .PSW(PSW), .intr(intr7__0),
    .ADDIVTP(INTRADDR), .CMEMBUS(pull_resistor_5_node), .CFFBUS(pull_resistor_7_node),
    .CREGBUS(pull_resistor_4_node), .rdMEM(out_9), .wrMEM(out_8), .UEXT2__0(UEXT2__0), .inta(inta),
    .INSTRUCBUS(common_1_instrucbus));

  // Other names for the same wires on the sheet: CLK = in_2; DIN7__0[7:0] = in_4; FCBUS = in_3; MAR[15:0] = ABUS;
  //   MDR[7:0] = DOUTBUS; RD = out_9; rst = in_1; WR = out_8
endmodule

module COMMON (
  input  CLK,
  input  ALUC,
  input  RST,
  input  [7:0] DIN,
  input  [15:0] A,
  input  [15:0] ALU,
  input  [15:0] IVTPPDSP,
  input  [14:0] CMEMBUS,
  input  [7:0] CFFBUS,
  input  [11:0] CREGBUS,
  input  [6:0] CPSW,
  output [15:0] MAR,
  output [7:0] MDR,
  output [3:0] PHASEFFBUS,
  output [20:0] INSTRUCBUS,
  output [6:0] ADDRBUS,
  output [15:0] PSW,
  output [15:0] B
);

  wire ADRINST, adrinst_t, and_1_out, and_2_out, and_3_out, and_4_out, and_5_out, and_6_out, and_7_out,
       and_8_out, and_9_out, and_10_out, and_11_out, and_12_out, and_13_out, and_14_out, and_15_out,
       and_16_out, and_17_out, and_18_out, and_19_out, and_20_out, and_21_out, and_22_out, and_23_out,
       and_24_out, and_25_out, and_26_out, and_27_out, and_28_out, and_29_out, and_30_out, and_31_out,
       and_32_out, and_33_out, bezadrinst, branchinst, jmpinst, not_1_out, not_2_out, not_3_out, not_4_out,
       not_5_out, not_6_out, not_7_out, not_8_out, not_9_out, not_10_out, or_1_out, or_2_out, or_3_out,
       or_4_out, or_5_out, or_6_out, or_7_out, or_8_out, or_9_out, or_10_out, or_11_out, or_12_out;
  wire [3:0] IR27__24;
  wire [7:0] DWH, DWL, IR7__0, IR15__8, IR23__16, mp2_16b_1_out_5, mp2_16b_1_out_5_2, mp4_8b_1_y, mp4_8b_2_y,
       mp8_8b_1_y;
  wire [7:4] IR31__24;
  wire [15:0] add16_1_f, ADDPCREL15__0, GPR15__0, mp2_16b_2_out_5, mp2_16b_3_out_5, mp4_16b_1_y, mp8_16b_1_y,
       PC15__0, SP15__0, sub16_1_f;

  REG8_LD reg8_ld_1 (.I7__0(MDR), .LD(CREGBUS[8]), .CLK(CLK), .A7__0({IR31__24, IR27__24}));  // open: mr
  REG8_LD reg8_ld_2 (.I7__0(MDR), .LD(CREGBUS[7]), .CLK(CLK), .A7__0(IR23__16));  // open: mr
  ADD16 add16_1 (.A(B), .B(16'h2), .F(add16_1_f));  // open: C0, C16
  DC4_16 dc4_16_1 (
    .En(PSW[0]), .X3__0(IR31__24), .D0(bezadrinst), .D1(branchinst), .D2(jmpinst), .D3(adrinst_t));  // open: D4, D5, D6, D7, D8, D9, D10, D11, D12, D13, D14, D15
  DC4_16 dc4_16_2 (
    .En(branchinst), .X3__0(IR27__24), .D0(INSTRUCBUS[8]), .D1(INSTRUCBUS[9]), .D2(INSTRUCBUS[10]),
    .D3(INSTRUCBUS[11]), .D4(INSTRUCBUS[12]));  // open: D5, D6, D7, D8, D9, D10, D11, D12, D13, D14, D15
  MP4_8b mp4_8b_1 (
    .S0(CREGBUS[2]), .S1(CREGBUS[3]), .I0(MDR), .I1(IR15__8), .I2(GPR15__0[15:8]), .I3(mp2_16b_1_out_5_2),
    .Y(mp4_8b_1_y), .En(1'b1));
  REG8_LD reg8_ld_3 (.I7__0(mp4_8b_1_y), .LD(CREGBUS[1]), .CLK(CLK), .A7__0(B[15:8]));  // open: mr
  ADD16 add16_2 (.A({{9{IR23__16[7]}}, IR23__16[6:0]}), .B(PC15__0), .F(ADDPCREL15__0));  // open: C0, C16
  MP8_16b mp8_16b_1 (
    .En(1'b1), .S0(CMEMBUS[5]), .S1(CMEMBUS[6]), .S2(CMEMBUS[14]), .I0(PC15__0), .I1({IR15__8, IR7__0}),
    .I2(B), .I3(SP15__0), .I4(GPR15__0), .I5(IVTPPDSP), .Y(mp8_16b_1_y));  // open: I6, I7
  REG16_INC_LD reg16_inc_ld_1 (
    .I15__0(mp8_16b_1_y), .LD(CMEMBUS[0]), .INC(CMEMBUS[1]), .CLK(CLK), .A15__0(MAR));  // open: mr
  MP2_16b mp2_16b_1 (
    .En(1'b1), .in_2(add16_1_f), .in_3(sub16_1_f), .S0(ADDRBUS[5]),
    .out_5({mp2_16b_1_out_5_2, mp2_16b_1_out_5}));
  REG8_LD reg8_ld_4 (.I7__0(MDR), .LD(CREGBUS[6]), .CLK(CLK), .A7__0(IR15__8));  // open: mr
  SUB16 sub16_1 (.A(B), .B(16'h2), .F(sub16_1_f));  // open: E0, E16
  MP4_8b mp4_8b_2 (
    .S0(CREGBUS[2]), .S1(CREGBUS[3]), .I0(MDR), .I1(IR7__0), .I2(GPR15__0[7:0]), .I3(mp2_16b_1_out_5),
    .Y(mp4_8b_2_y), .En(1'b1));
  REG8_LD reg8_ld_5 (.I7__0(mp4_8b_2_y), .LD(CREGBUS[0]), .CLK(CLK), .A7__0(B[7:0]));  // open: mr
  DC4_16 dc4_16_3 (
    .En(bezadrinst), .X3__0(IR27__24), .D0(INSTRUCBUS[0]), .D1(INSTRUCBUS[1]), .D2(INSTRUCBUS[2]),
    .D3(INSTRUCBUS[3]), .D4(INSTRUCBUS[4]), .D5(INSTRUCBUS[5]), .D6(INSTRUCBUS[6]), .D7(INSTRUCBUS[7]));  // open: D8, D9, D10, D11, D12, D13, D14, D15
  DC4_16 dc4_16_4 (
    .En(jmpinst), .X3__0(IR27__24), .D0(INSTRUCBUS[13]), .D1(INSTRUCBUS[14]), .D2(INSTRUCBUS[15]));  // open: D3, D4, D5, D6, D7, D8, D9, D10, D11, D12, D13, D14, D15
  MP8_8b mp8_8b_1 (
    .En(1'b1), .S0(CMEMBUS[7]), .S1(CMEMBUS[8]), .S2(CMEMBUS[9]), .I0(DIN), .I1(A[7:0]), .I2(PC15__0[15:8]),
    .I3(PC15__0[7:0]), .I4(PSW[7:0]), .I5(A[15:8]), .I6(PSW[15:8]), .Y(mp8_8b_1_y));  // open: I7
  REG8_LD reg8_ld_6 (.I7__0(mp8_8b_1_y), .LD(CMEMBUS[2]), .CLK(CLK), .A7__0(MDR));  // open: mr
  REG8_LD reg8_ld_7 (.I7__0(MDR), .LD(CREGBUS[5]), .CLK(CLK), .A7__0(IR7__0));  // open: mr
  REG8_LD reg8_ld_8 (.I7__0(MDR), .LD(CREGBUS[10]), .CLK(CLK), .A7__0(DWH));  // open: mr
  MP4_16b mp4_16b_1 (
    .En(1'b1), .S0(CMEMBUS[13]), .S1(CMEMBUS[12]), .I0({IR23__16, IR15__8}), .I1(ADDPCREL15__0),
    .I2({DWH, DWL}), .Y(mp4_16b_1_y));  // open: I3
  DC4_16 dc4_16_5 (
    .En(adrinst_t), .X3__0(IR27__24), .D0(INSTRUCBUS[16]), .D1(INSTRUCBUS[17]), .D2(INSTRUCBUS[18]),
    .D3(INSTRUCBUS[19]), .D4(INSTRUCBUS[20]));  // open: D5, D6, D7, D8, D9, D10, D11, D12, D13, D14, D15
  DC4_16 dc4_16_6 (
    .En(adrinst_t), .X3__0(IR23__16[7:4]), .D0(ADDRBUS[0]), .D1(ADDRBUS[1]), .D2(ADDRBUS[2]),
    .D3(ADDRBUS[3]), .D4(ADDRBUS[4]), .D5(ADDRBUS[5]), .D6(ADDRBUS[6]));  // open: D7, D8, D9, D10, D11, D12, D13, D14, D15
  not not_1 (not_1_out, RST);
  RSFF rsff_1 (.S(CFFBUS[0]), .CLK(CLK), .R(CFFBUS[1]), .Sd(not_1_out), .Q(PHASEFFBUS[0]));  // open: Rd, notQ
  MP2_16b mp2_16b_2 (.En(1'b1), .in_2(mp4_16b_1_y), .in_3(16'h1000), .S0(RST), .out_5(mp2_16b_2_out_5));
  REG16_INC_LD reg16_inc_ld_2 (
    .I15__0(mp2_16b_2_out_5), .LD(or_1_out), .INC(CMEMBUS[4]), .CLK(CLK), .A15__0(PC15__0));  // open: mr
  REG16 reg16_1 (
    .LD(RST), .A(16'hf000), .DEC(CMEMBUS[11]), .INC(CMEMBUS[10]), .CLK(CLK), .I(SP15__0));  // open: CL, SL, IL, SR, IR, Cout, Eout, mr
  or or_1 (or_1_out, CMEMBUS[3], RST);
  REG8_LD reg8_ld_9 (.I7__0(MDR), .LD(CREGBUS[9]), .CLK(CLK), .A7__0(DWL));  // open: mr
  RSFF rsff_2 (.S(CFFBUS[2]), .CLK(CLK), .R(CFFBUS[3]), .Rd(not_2_out), .Q(PHASEFFBUS[1]));  // open: Sd, notQ
  not not_2 (not_2_out, RST);
  or or_2 (or_2_out, ADRINST, INSTRUCBUS[5], INSTRUCBUS[7], INSTRUCBUS[6]);
  or or_3 (or_3_out, ADRINST, INSTRUCBUS[5], INSTRUCBUS[7], INSTRUCBUS[6]);
  and and_1 (and_1_out, ~A[15], ~B[15], ALU[15]);  // AND_Gate
  or or_4 (or_4_out, and_1_out, and_2_out);
  and and_2 (and_2_out, A[15], B[15], ~ALU[15]);  // AND_Gate
  and and_3 (and_3_out, ~A[15], B[15], ALU[15]);  // AND_Gate
  or or_5 (or_5_out, and_3_out, and_4_out);
  and and_4 (and_4_out, A[15], ~B[15], ~ALU[15]);  // AND_Gate
  and and_5 (and_5_out, ~A[15], ALU[15]);  // AND_Gate
  or or_6 (or_6_out, INSTRUCBUS[18], INSTRUCBUS[7]);
  and and_6 (and_6_out, or_6_out, ALUC);
  and and_7 (and_7_out, INSTRUCBUS[19], ALUC);
  RSFF rsff_3 (.S(CFFBUS[4]), .CLK(CLK), .R(CFFBUS[5]), .Rd(not_3_out), .Q(PHASEFFBUS[2]));  // open: Sd, notQ
  not not_3 (not_3_out, RST);
  and and_8 (and_8_out, MDR[1], INSTRUCBUS[2]);
  and and_9 (and_9_out, or_2_out, and_10_out);
  and and_10 (and_10_out, ~A[0], ~A[1], ~A[2], ~A[3], ~A[4], ~A[5], ~A[6], ~A[7], ~A[8], ~A[9], ~A[10], ~A[11], ~A[12], ~A[13], ~A[14], ~A[15]);  // AND_Gate
  and and_11 (and_11_out, MDR[2], INSTRUCBUS[2]);
  and and_12 (and_12_out, or_3_out, A[15]);
  and and_13 (and_13_out, MDR[3], INSTRUCBUS[2]);
  and and_14 (and_14_out, INSTRUCBUS[19], or_4_out);
  or or_7 (or_7_out, and_14_out, and_15_out, and_16_out);
  and and_15 (and_15_out, INSTRUCBUS[18], or_5_out);
  and and_16 (and_16_out, INSTRUCBUS[7], and_5_out);
  and and_17 (and_17_out, INSTRUCBUS[6], A[0]);
  and and_18 (and_18_out, MDR[4], INSTRUCBUS[2]);
  and and_19 (and_19_out, ADRINST, A[15]);
  and and_20 (and_20_out, INSTRUCBUS[5], A[15]);
  and and_21 (and_21_out, MDR[7], INSTRUCBUS[2]);
  and and_22 (and_22_out, ~MDR[0], INSTRUCBUS[2], CPSW[6]);  // AND_Gate
  or or_8 (or_8_out, and_22_out, CPSW[0]);
  and and_23 (and_23_out, MDR[0], INSTRUCBUS[2], CPSW[6]);
  or or_9 (or_9_out, and_8_out, and_9_out);
  or or_10 (or_10_out, and_11_out, and_12_out);
  or or_11 (or_11_out, and_13_out, or_7_out);
  or or_12 (or_12_out, and_17_out, and_18_out, and_6_out, and_7_out, and_19_out, and_20_out);
  MP2_16b mp2_16b_3 (.En(1'b1), .in_2(A), .in_3(B), .S0(CREGBUS[11]), .out_5(mp2_16b_3_out_5));
  GPR16x16 gpr16x16_1 (
    .DI15__0(mp2_16b_3_out_5), .A3__0(IR23__16[3:0]), .WR(CREGBUS[4]), .CLK(CLK), .DO15__0(GPR15__0));
  not not_4 (not_4_out, RST);
  RSFF rsff_4 (.S(and_23_out), .CLK(CLK), .R(or_8_out), .Sd(not_4_out), .Q(PSW[0]));  // open: Rd, notQ
  and and_24 (and_24_out, ~or_9_out, CPSW[4]);  // AND_Gate
  and and_25 (and_25_out, or_9_out, CPSW[4]);
  and and_26 (and_26_out, ~or_10_out, CPSW[3]);  // AND_Gate
  and and_27 (and_27_out, or_10_out, CPSW[3]);
  and and_28 (and_28_out, ~or_12_out, CPSW[5]);  // AND_Gate
  and and_29 (and_29_out, or_12_out, CPSW[5]);
  not not_5 (not_5_out, RST);
  and and_30 (and_30_out, ~and_21_out, CPSW[1]);  // AND_Gate
  RSFF rsff_5 (.S(and_31_out), .CLK(CLK), .R(and_30_out), .Sd(not_5_out), .Q(PSW[15]));  // open: Rd, notQ
  and and_31 (and_31_out, and_21_out, CPSW[1]);
  RSFF rsff_6 (.S(CFFBUS[6]), .CLK(CLK), .R(CFFBUS[7]), .Rd(not_6_out), .Q(PHASEFFBUS[3]));  // open: Sd, notQ
  not not_6 (not_6_out, RST);
  or or_13 (ADRINST, INSTRUCBUS[16], INSTRUCBUS[19], INSTRUCBUS[18]);
  RSFF rsff_7 (.S(and_25_out), .CLK(CLK), .R(and_24_out), .Rd(not_7_out), .Q(PSW[1]));  // open: Sd, notQ
  not not_7 (not_7_out, RST);
  RSFF rsff_8 (.S(and_27_out), .CLK(CLK), .R(and_26_out), .Rd(not_8_out), .Q(PSW[2]));  // open: Sd, notQ
  not not_8 (not_8_out, RST);
  and and_32 (and_32_out, ~or_11_out, CPSW[2]);  // AND_Gate
  RSFF rsff_9 (.S(and_33_out), .CLK(CLK), .R(and_32_out), .Rd(not_9_out), .Q(PSW[3]));  // open: Sd, notQ
  not not_9 (not_9_out, RST);
  and and_33 (and_33_out, or_11_out, CPSW[2]);
  RSFF rsff_10 (.S(and_29_out), .CLK(CLK), .R(and_28_out), .Rd(not_10_out), .Q(PSW[4]));  // open: Sd, notQ
  not not_10 (not_10_out, RST);

  // Other names for the same wires on the sheet: A7__0[7:0] = A[7:0]; A15__0[15:0] = A; A15__8[7:0] = A[15:8];
  //   immed = ADDRBUS[0]; memdir = ADDRBUS[1]; memind = ADDRBUS[2]; regind = ADDRBUS[3]; regdir = ADDRBUS[4];
  //   predec = ADDRBUS[5]; preinc = ADDRBUS[6]; ALU15__0[15:0] = ALU; B7__0[7:0] = B[7:0]; B15__0[15:0] = B;
  //   B15__8[7:0] = B[15:8]; stFETCH = CFFBUS[0]; clFETCH = CFFBUS[1]; stADDR = CFFBUS[2]; clADDR = CFFBUS[3];
  //   stEXEC = CFFBUS[4]; clEXEC = CFFBUS[5]; stINTR = CFFBUS[6]; clINTR = CFFBUS[7]; ldMAR = CMEMBUS[0];
  //   incMAR = CMEMBUS[1]; ldMDR = CMEMBUS[2]; ldPC = CMEMBUS[3]; incPC = CMEMBUS[4]; mxMAR0 = CMEMBUS[5];
  //   mxMAR1 = CMEMBUS[6]; mxMDR0 = CMEMBUS[7]; mxMDR1 = CMEMBUS[8]; mxMDR2 = CMEMBUS[9]; incSP = CMEMBUS[10];
  //   decSP = CMEMBUS[11]; mxPC1 = CMEMBUS[12]; mxPC0 = CMEMBUS[13]; mxMAR2 = CMEMBUS[14]; clPSWSTART = CPSW[0];
  //   ldI = CPSW[1]; ldV = CPSW[2]; ldN = CPSW[3]; ldZ = CPSW[4]; ldC = CPSW[5]; ldSTART = CPSW[6];
  //   ldB7__0 = CREGBUS[0]; ldB15__8 = CREGBUS[1]; mxB0 = CREGBUS[2]; mxB1 = CREGBUS[3]; wrGPR = CREGBUS[4];
  //   ldIR7__0 = CREGBUS[5]; ldIR15__8 = CREGBUS[6]; ldIR23__16 = CREGBUS[7]; ldIR31__24 = CREGBUS[8];
  //   ldDWL = CREGBUS[9]; ldDWH = CREGBUS[10]; mxGPR = CREGBUS[11]; Din7__0[7:0] = DIN;
  //   ENTRADDR15__0[15:0] = IVTPPDSP; HALT = INSTRUCBUS[0]; RTS = INSTRUCBUS[1]; RTI = INSTRUCBUS[2];
  //   INTE = INSTRUCBUS[3]; INTD = INSTRUCBUS[4]; ROL = INSTRUCBUS[5]; ROR = INSTRUCBUS[6]; DEC = INSTRUCBUS[7];
  //   BLEQ = INSTRUCBUS[8]; BNVF = INSTRUCBUS[9]; BLSSU = INSTRUCBUS[10]; BOVF = INSTRUCBUS[11];
  //   JEQL = INSTRUCBUS[12]; BR = INSTRUCBUS[13]; JMP = INSTRUCBUS[14]; JSR = INSTRUCBUS[15]; LD = INSTRUCBUS[16];
  //   ST = INSTRUCBUS[17]; SUB = INSTRUCBUS[18]; ADD = INSTRUCBUS[19]; MUL = INSTRUCBUS[20]; IR31__24[3:0] = IR27__24;
  //   MAR15__0[15:0] = MAR; MDR7__0[7:0] = MDR; FETCH = PHASEFFBUS[0]; ADDR = PHASEFFBUS[1]; EXEC = PHASEFFBUS[2];
  //   INTR = PHASEFFBUS[3]; PSW15__0[15:0] = PSW; PSWSTART = PSW[0]; PSWZ = PSW[1]; PSWN = PSW[2]; PSWV = PSW[3];
  //   PSWC = PSW[4]; PSWI = PSW[15]

  // Notes on the sheet:
  //   Sabirac
  //   Instrukcijski registar
  //   Pomocni registri
  //   MAR
  //   Dekoderi za prepoznavanje instrukcije na osnovu sadrzaja registra IR31..24
  //   MDR
  //   SP
  //   PC
  //   Dekoderi za prepoznavanje nacina adresiranja
  //   FF za pokretanje FETCH, ADDR, EXEC i INTR faze izvršavanja instrukcije
  //   Registarski fajl
  //   Programska statusna reč (PSW)
endmodule

module FETCH (
  input  in_1,
  input  in_2,
  input  in_3,
  input  [3:0] PHASEFFBUS,
  input  [20:0] INSTRUCBUS,
  input  [15:0] PSW,
  input  [6:0] ADDRBUS,
  output [14:0] CMEMBUS,
  output [7:0] CFFBUS,
  output [11:0] CREGBUS,
  output rdMEM
);

  wire addr2, addr4, addr_t, and_4_out, and_5_out, and_6_out, and_7_out, and_8_out, and_9_out, and_10_out,
       and_11_out, and_12_out, and_13_out, bezadr1, braddr2, branch2, brbezadr1, brbranch2, brcnd, brgradr,
       brgropr, brjmp3, brnotfcmem, bruncnd, clFETCH, gradr, gropr, incPC, jmp3, ldIR7__0, ldIR15__8,
       ldIR23__16, ldIR31__24, ldMAR, ldMDR, not_1_out, not_2_out, not_3_out, not_4_out, not_5_out,
       notPSWSTandFETCH, or_4_out, or_5_out, or_6_out, or_9_out, rdMEM_t, stADDR, stEXEC;
  wire [3:0] rom32x24_1_dout_2;
  wire [7:0] reg8_inc_ld_1_a7__0, rom32x24_1_dout;
  wire [11:11] rom32x24_1_dout_3;

  or or_1 (bezadr1, INSTRUCBUS[0], INSTRUCBUS[1], INSTRUCBUS[2], INSTRUCBUS[3], INSTRUCBUS[4], INSTRUCBUS[5], INSTRUCBUS[6], INSTRUCBUS[7]);
  or or_2 (branch2, INSTRUCBUS[8], INSTRUCBUS[9], INSTRUCBUS[10], INSTRUCBUS[11], INSTRUCBUS[13]);
  or or_3 (jmp3, INSTRUCBUS[12], INSTRUCBUS[14], INSTRUCBUS[15]);
  not not_1 (not_1_out, in_1);
  REG8_INC_LD reg8_inc_ld_1 (
    .I7__0(rom32x24_1_dout), .LD(or_4_out), .INC(not_2_out), .mr(not_1_out), .CLK(in_2),
    .A7__0(reg8_inc_ld_1_a7__0));
  not not_2 (not_2_out, or_4_out);
  ROM32x24 rom32x24_1 (
    .A4__0(reg8_inc_ld_1_a7__0[4:0]), .CS(1'b1),
    .DOUT({rom32x24_1_dout, rom32x24_1_dout_2, rom32x24_1_dout_3[11], stEXEC, stADDR, clFETCH, ldIR7__0, ldIR15__8, ldIR23__16, ldIR31__24, ldMDR, rdMEM_t, incPC, ldMAR}));
  DC4_16 dc4_16_1 (
    .En(1'b1), .X3__0(rom32x24_1_dout_2), .D1(bruncnd), .D2(notPSWSTandFETCH), .D3(brbezadr1),
    .D4(brbranch2), .D5(braddr2), .D6(brjmp3), .D7(brgropr), .D8(brgradr), .D9(brnotfcmem));  // open: D0, D10, D11, D12, D13, D14, D15
  or or_4 (or_4_out, bruncnd, brcnd);
  or or_5 (or_5_out, ADDRBUS[0], ADDRBUS[1], ADDRBUS[2]);
  or or_6 (or_6_out, ADDRBUS[4], ADDRBUS[3], ADDRBUS[5], ADDRBUS[6]);
  or or_7 (addr_t, INSTRUCBUS[16], INSTRUCBUS[17], INSTRUCBUS[19], INSTRUCBUS[18], INSTRUCBUS[20]);
  and and_1 (addr4, addr_t, or_5_out);
  and and_2 (addr2, addr_t, or_6_out);
  and and_3 (gropr, ~bezadr1, ~branch2, ~jmp3, ~addr_t);  // AND_Gate
  and and_4 (and_4_out, addr_t, ~addr4, ~addr2);  // AND_Gate
  and and_5 (and_5_out, INSTRUCBUS[17], ADDRBUS[0]);
  not not_3 (not_3_out, PHASEFFBUS[0]);
  not not_4 (not_4_out, PSW[0]);
  or or_8 (gradr, and_4_out, and_5_out);
  or or_9 (or_9_out, not_3_out, not_4_out);
  not not_5 (not_5_out, in_3);
  and and_6 (and_6_out, brgropr, gropr);
  and and_7 (and_7_out, or_9_out, notPSWSTandFETCH);
  and and_8 (and_8_out, brbezadr1, bezadr1);
  and and_9 (and_9_out, brbranch2, branch2);
  and and_10 (and_10_out, braddr2, addr2);
  and and_11 (and_11_out, brjmp3, jmp3);
  and and_12 (and_12_out, brnotfcmem, not_5_out);
  and and_13 (and_13_out, brgradr, gradr);
  or or_10 (brcnd, and_6_out, and_7_out, and_8_out, and_9_out, and_10_out, and_11_out, and_12_out, and_13_out);
  assign CMEMBUS[0] = ldMAR ? 1'b1 : 1'bz;  // Controlled_Buffer controlled_buffer_1
  assign CMEMBUS[2] = ldMDR ? 1'b1 : 1'bz;  // Controlled_Buffer controlled_buffer_2
  assign CMEMBUS[4] = incPC ? 1'b1 : 1'bz;  // Controlled_Buffer controlled_buffer_3
  assign CFFBUS[1] = clFETCH ? 1'b1 : 1'bz;  // Controlled_Buffer controlled_buffer_4
  assign CFFBUS[2] = stADDR ? 1'b1 : 1'bz;  // Controlled_Buffer controlled_buffer_5
  assign CFFBUS[4] = stEXEC ? 1'b1 : 1'bz;  // Controlled_Buffer controlled_buffer_6
  assign CREGBUS[5] = ldIR7__0 ? 1'b1 : 1'bz;  // Controlled_Buffer controlled_buffer_7
  assign CREGBUS[6] = ldIR15__8 ? 1'b1 : 1'bz;  // Controlled_Buffer controlled_buffer_8
  assign CREGBUS[7] = ldIR23__16 ? 1'b1 : 1'bz;  // Controlled_Buffer controlled_buffer_9
  assign CREGBUS[8] = ldIR31__24 ? 1'b1 : 1'bz;  // Controlled_Buffer controlled_buffer_10
  assign rdMEM = rdMEM_t ? 1'b1 : 1'bz;  // Controlled_Buffer controlled_buffer_11

  // Other names for the same wires on the sheet: immed = ADDRBUS[0]; memdir = ADDRBUS[1]; memind = ADDRBUS[2];
  //   regind = ADDRBUS[3]; regdir = ADDRBUS[4]; predec = ADDRBUS[5]; preinc = ADDRBUS[6]; CLK = in_2; FCBUS = in_3;
  //   HALT = INSTRUCBUS[0]; RTS = INSTRUCBUS[1]; RTI = INSTRUCBUS[2]; INTE = INSTRUCBUS[3]; INTD = INSTRUCBUS[4];
  //   ROL = INSTRUCBUS[5]; ROR = INSTRUCBUS[6]; DEC = INSTRUCBUS[7]; BLEQ = INSTRUCBUS[8]; BNVF = INSTRUCBUS[9];
  //   BLSSU = INSTRUCBUS[10]; BOVF = INSTRUCBUS[11]; JEQL = INSTRUCBUS[12]; BR = INSTRUCBUS[13]; JMP = INSTRUCBUS[14];
  //   JSR = INSTRUCBUS[15]; LD = INSTRUCBUS[16]; ST = INSTRUCBUS[17]; SUB = INSTRUCBUS[18]; ADD = INSTRUCBUS[19];
  //   MUL = INSTRUCBUS[20]; FETCH = PHASEFFBUS[0]; ADDR = PHASEFFBUS[1]; EXEC = PHASEFFBUS[2]; INTR = PHASEFFBUS[3];
  //   PSWSTART = PSW[0]; rst = in_1

  // Notes on the sheet:
  //   Operaciona jedinica
  //   Kontrolna jedinica
endmodule

module ADDR (
  input  in_1,
  input  in_2,
  input  in_3,
  input  [3:0] PHASEFFBUS,
  input  [6:0] ADDRBUS,
  input  [20:0] INSTRUCBUS,
  output [14:0] CMEMBUS,
  output [7:0] CFFBUS,
  output [11:0] CREGBUS,
  output rdMEM
);

  wire and_1_out, and_2_out, and_3_out, and_4_out, bradr, brcnd, brJEQL, brnotADDR, brnotfcbus, brSTORE,
       bruncnd, clADDR, incMAR, ldB7__0, ldB15__8, ldMAR, ldMDR, mxB0, mxB1, mxGPR, mxMAR0, mxMAR1, mxMAR2,
       not_1_out, not_2_out, not_3_out, not_4_out, or_1_out, rdMEM_t, stEXEC, wrGPR;
  wire [4:0] kmadr_1_adr4__0, rom32x24v2_1_dout;
  wire [7:0] mp2_8b_1_out_5, reg8_inc_ld_1_a7__0;
  wire [18:15] rom32x24v2_1_dout_2;

  not not_1 (not_1_out, in_1);
  DC3_8 dc3_8_1 (
    .En(1'b1), .X2__0(rom32x24v2_1_dout_2[18:16]), .D1(bruncnd), .D2(brnotADDR), .D3(brSTORE), .D4(brJEQL),
    .D5(brnotfcbus), .D6(bradr));  // open: D0, D7
  KMADR kmadr_1 (
    .immed(ADDRBUS[0]), .memdir(ADDRBUS[1]), .memind(ADDRBUS[2]), .regind(ADDRBUS[3]),
    .Adr4__0(kmadr_1_adr4__0), .regdir(ADDRBUS[4]), .predec(ADDRBUS[5]), .preinc(ADDRBUS[6]));
  MP2_8b mp2_8b_1 (
    .in_2({3'b000, rom32x24v2_1_dout}), .in_3({3'b000, kmadr_1_adr4__0}), .S0(bradr), .out_5(mp2_8b_1_out_5),
    .En(1'b1));
  REG8_INC_LD reg8_inc_ld_1 (
    .I7__0(mp2_8b_1_out_5), .LD(or_1_out), .INC(not_2_out), .mr(not_1_out), .CLK(in_2),
    .A7__0(reg8_inc_ld_1_a7__0));
  not not_2 (not_2_out, or_1_out);
  ROM32x24v2 rom32x24v2_1 (
    .A4__0(reg8_inc_ld_1_a7__0[4:0]), .CS(1'b1),
    .DOUT({rom32x24v2_1_dout, rom32x24v2_1_dout_2, stEXEC, clADDR, incMAR, mxGPR, wrGPR, ldMDR, rdMEM_t, mxMAR1, mxB1, mxMAR0, ldMAR, mxB0, ldB15__8, ldB7__0, mxMAR2}));
  or or_1 (or_1_out, bruncnd, brcnd, bradr);
  not not_3 (not_3_out, PHASEFFBUS[1]);
  not not_4 (not_4_out, in_3);
  and and_1 (and_1_out, not_3_out, brnotADDR);
  and and_2 (and_2_out, INSTRUCBUS[17], brSTORE);
  and and_3 (and_3_out, INSTRUCBUS[12], brJEQL);
  and and_4 (and_4_out, brnotfcbus, not_4_out);
  or or_2 (brcnd, and_1_out, and_2_out, and_3_out, and_4_out);
  assign CMEMBUS[0] = ldMAR ? 1'b1 : 1'bz;  // Controlled_Buffer controlled_buffer_1
  assign CMEMBUS[1] = incMAR ? 1'b1 : 1'bz;  // Controlled_Buffer controlled_buffer_2
  assign CMEMBUS[2] = ldMDR ? 1'b1 : 1'bz;  // Controlled_Buffer controlled_buffer_3
  assign CMEMBUS[5] = mxMAR0 ? 1'b1 : 1'bz;  // Controlled_Buffer controlled_buffer_4
  assign CMEMBUS[6] = mxMAR1 ? 1'b1 : 1'bz;  // Controlled_Buffer controlled_buffer_5
  assign CMEMBUS[14] = mxMAR2 ? 1'b1 : 1'bz;  // Controlled_Buffer controlled_buffer_6
  assign CFFBUS[3] = clADDR ? 1'b1 : 1'bz;  // Controlled_Buffer controlled_buffer_7
  assign CFFBUS[4] = stEXEC ? 1'b1 : 1'bz;  // Controlled_Buffer controlled_buffer_8
  assign CREGBUS[0] = ldB7__0 ? 1'b1 : 1'bz;  // Controlled_Buffer controlled_buffer_9
  assign CREGBUS[1] = ldB15__8 ? 1'b1 : 1'bz;  // Controlled_Buffer controlled_buffer_10
  assign CREGBUS[2] = mxB0 ? 1'b1 : 1'bz;  // Controlled_Buffer controlled_buffer_11
  assign CREGBUS[3] = mxB1 ? 1'b1 : 1'bz;  // Controlled_Buffer controlled_buffer_12
  assign CREGBUS[4] = wrGPR ? 1'b1 : 1'bz;  // Controlled_Buffer controlled_buffer_13
  assign rdMEM = rdMEM_t ? 1'b1 : 1'bz;  // Controlled_Buffer controlled_buffer_14

  // Other names for the same wires on the sheet: immed = ADDRBUS[0]; memdir = ADDRBUS[1]; memind = ADDRBUS[2];
  //   regind = ADDRBUS[3]; regdir = ADDRBUS[4]; predec = ADDRBUS[5]; preinc = ADDRBUS[6]; CLK = in_2; FCBUS = in_3;
  //   JEQL = INSTRUCBUS[12]; ST = INSTRUCBUS[17]; ADDR = PHASEFFBUS[1]; rst = in_1

  // Notes on the sheet:
  //   Operaciona jedinica
  //   Upravljacka jedinica
endmodule

module EXEC (
  input  in_1,
  input  in_2,
  input  in_3,
  input  [15:0] B,
  input  [3:0] PHASEFFBUS,
  input  [6:0] ADDRBUS,
  input  [15:0] PSW,
  input  [20:0] INSTRUCBUS,
  output ALUC,
  output [15:0] A,
  output [15:0] ALU,
  output [14:0] CMEMBUS,
  output [7:0] CFFBUS,
  output [11:0] CREGBUS,
  output [6:0] CPSW,
  output rdMEM,
  output wrMEM
);

  wire add_t, and_1_out, and_2_out, and_3_out, and_4_out, and_5_out, and_6_out, and_7_out, and_8_out,
       and_9_out, and_10_out, and_11_out, and_12_out, and_13_out, and_14_out, brcnd, brimmed, brnotC,
       brnotEXEC, brnotFCBUS, brnotsignal1, brnotV, brnotZ, bropr, brorjmp, brregdir, bruncnd, brV, clEXEC,
       clI, clPSWSTART, decA, decSP, incMAR, incSP, ldA, ldC, ldDWH, ldDWL, ldI, ldMAR, ldMDR, ldN, ldPC,
       ldSTART, ldV, ldZ, mul_t, mxA0, mxALU, mxMAR0, mxMAR1, mxMDR0, mxMDR1, mxMDR2, mxPC0, mxPC1,
       not_1_out, not_2_out, not_3_out, not_4_out, not_5_out, not_6_out, not_7_out, not_8_out, not_9_out,
       or_1_out, rdMEM_t, signal1, slA, srA, stI, stINTR, sub_t, wrGPR, wrMEM_t, xor_1_out;
  wire [3:0] rom64x52_1_dout51__32_2;
  wire [5:0] kmopr_1_adr5__0, mp2_6b_1_y, reg6_inc_ld_1_a5__0, rom64x52_1_dout51__32;
  wire [9:6] rom64x52_1_dout51__32_3;
  wire [15:0] mp2_16b_1_out_5, mp2_16b_2_out_5;

  DC4_16 dc4_16_1 (
    .En(1'b1), .X3__0(rom64x52_1_dout51__32_2), .D1(bruncnd), .D2(brnotEXEC), .D3(bropr), .D4(brnotFCBUS),
    .D5(brnotsignal1), .D6(brV), .D7(brnotC), .D8(brnotV), .D9(brnotZ), .D10(brimmed), .D11(brregdir));  // open: D0, D12, D13, D14, D15
  MP2_16b mp2_16b_1 (.En(1'b1), .in_2(B), .in_3(ALU), .S0(mxA0), .out_5(mp2_16b_1_out_5));
  not not_1 (not_1_out, in_1);
  REG16_LD_SR_SL reg16_ld_sr_sl_1 (
    .I15__0(mp2_16b_1_out_5), .LD(ldA), .IR(A[15]), .SR(srA), .IL(A[0]), .SL(slA), .mr(not_1_out),
    .CLK(in_2), .A15__0(A));
  not not_2 (not_2_out, in_1);
  MP2_6b mp2_6b_1 (.En(1'b1), ._5__0(rom64x52_1_dout51__32), .in_3(kmopr_1_adr5__0), .S0(bropr), .Y(mp2_6b_1_y));
  REG6_INC_LD reg6_inc_ld_1 (
    .I5__0(mp2_6b_1_y), .LD(or_1_out), .INC(not_3_out), .mr(not_2_out), .CLK(in_2),
    .A5__0(reg6_inc_ld_1_a5__0));
  not not_3 (not_3_out, or_1_out);
  ROM64x52 rom64x52_1 (
    .A5__0(reg6_inc_ld_1_a5__0), .CS(1'b1),
    .DOUT51__32({rom64x52_1_dout51__32, rom64x52_1_dout51__32_2, rom64x52_1_dout51__32_3, mxALU, mxA0, clPSWSTART, incSP, ldMAR, ldMDR}),
    .DOUT31__0({rdMEM_t, ldPC, stI, clI, slA, srA, decA, ldN, ldZ, decSP, wrMEM_t, ldA, wrGPR, ldV, ldC, ldI, mxMAR0, mxMAR1, ldDWH, ldDWL, mxPC1, mxPC0, mxMDR0, mxMDR2, sub_t, add_t, mul_t, clEXEC, stINTR, mxMDR1, incMAR, ldSTART}));
  KMOPR kmopr_1 (
    .LD(INSTRUCBUS[16]), .ST(INSTRUCBUS[17]), .SUB(INSTRUCBUS[18]), .ADD(INSTRUCBUS[19]),
    .MUL(INSTRUCBUS[20]), .Adr5__0(kmopr_1_adr5__0), .HALT(INSTRUCBUS[0]), .RTS(INSTRUCBUS[1]),
    .RTI(INSTRUCBUS[2]), .INTE(INSTRUCBUS[3]), .INTD(INSTRUCBUS[4]), .ROL(INSTRUCBUS[5]),
    .ROR(INSTRUCBUS[6]), .DEC(INSTRUCBUS[7]), .BLEQ(INSTRUCBUS[8]), .BNVF(INSTRUCBUS[9]),
    .BLSSU(INSTRUCBUS[10]), .BOVF(INSTRUCBUS[11]), .JEQL(INSTRUCBUS[12]), .JMP(INSTRUCBUS[14]),
    .JSR(INSTRUCBUS[15]), .BR(INSTRUCBUS[13]));
  or or_1 (or_1_out, bruncnd, brcnd, bropr);
  ALU16_ADD_SUB alu16_add_sub_1 (
    .Cin(1'b0), .A(A), .B(mp2_16b_2_out_5), .add(add_t), .sub(sub_t), .F(ALU), .Cout(ALUC), .mul(mul_t));
  MP2_16b mp2_16b_2 (.En(1'b1), .in_2(B), .in_3(16'h1), .S0(mxALU), .out_5(mp2_16b_2_out_5));
  xor xor_1 (xor_1_out, PSW[2], PSW[3]);
  not not_4 (not_4_out, PHASEFFBUS[2]);
  not not_5 (not_5_out, in_3);
  not not_6 (not_6_out, PSW[4]);
  not not_7 (not_7_out, PSW[3]);
  not not_8 (not_8_out, PSW[1]);
  not not_9 (not_9_out, PSW[3]);
  or or_2 (signal1, xor_1_out, PSW[1]);
  and and_1 (and_1_out, not_4_out, brnotEXEC);
  and and_2 (and_2_out, signal1, brnotsignal1);
  and and_3 (and_3_out, not_5_out, brnotFCBUS);
  and and_4 (and_4_out, PSW[3], brV);
  and and_5 (and_5_out, not_6_out, brnotC);
  and and_6 (and_6_out, not_7_out, brnotV);
  and and_7 (and_7_out, not_8_out, brnotZ);
  and and_8 (and_8_out, ADDRBUS[0], brimmed);
  and and_9 (and_9_out, ADDRBUS[4], brregdir);
  and and_10 (and_10_out, signal1, INSTRUCBUS[8]);
  and and_11 (and_11_out, not_9_out, INSTRUCBUS[9]);
  and and_12 (and_12_out, PSW[4], INSTRUCBUS[10]);
  and and_13 (and_13_out, PSW[3], INSTRUCBUS[11]);
  and and_14 (and_14_out, PSW[1], INSTRUCBUS[12]);
  or or_3 (brorjmp, and_10_out, and_11_out, and_12_out, and_13_out, and_14_out);
  or or_4 (brcnd, and_1_out, and_2_out, and_3_out, and_4_out, and_5_out, and_6_out, and_7_out, and_8_out, and_9_out);
  assign CMEMBUS[9] = mxMDR2 ? 1'b1 : 1'bz;  // Controlled_Buffer controlled_buffer_1
  assign CMEMBUS[1] = incMAR ? 1'b1 : 1'bz;  // Controlled_Buffer controlled_buffer_2
  assign CMEMBUS[0] = ldMAR ? 1'b1 : 1'bz;  // Controlled_Buffer controlled_buffer_3
  assign CMEMBUS[2] = ldMDR ? 1'b1 : 1'bz;  // Controlled_Buffer controlled_buffer_4
  assign CMEMBUS[3] = ldPC ? 1'b1 : 1'bz;  // Controlled_Buffer controlled_buffer_5
  assign CMEMBUS[5] = mxMAR0 ? 1'b1 : 1'bz;  // Controlled_Buffer controlled_buffer_6
  assign CMEMBUS[6] = mxMAR1 ? 1'b1 : 1'bz;  // Controlled_Buffer controlled_buffer_7
  assign CMEMBUS[7] = mxMDR0 ? 1'b1 : 1'bz;  // Controlled_Buffer controlled_buffer_8
  assign CMEMBUS[8] = mxMDR1 ? 1'b1 : 1'bz;  // Controlled_Buffer controlled_buffer_9
  assign CMEMBUS[10] = incSP ? 1'b1 : 1'bz;  // Controlled_Buffer controlled_buffer_10
  assign CMEMBUS[11] = decSP ? 1'b1 : 1'bz;  // Controlled_Buffer controlled_buffer_11
  assign CMEMBUS[12] = mxPC1 ? 1'b1 : 1'bz;  // Controlled_Buffer controlled_buffer_12
  assign CMEMBUS[13] = mxPC0 ? 1'b1 : 1'bz;  // Controlled_Buffer controlled_buffer_13
  assign CFFBUS[5] = clEXEC ? 1'b1 : 1'bz;  // Controlled_Buffer controlled_buffer_14
  assign CFFBUS[6] = stINTR ? 1'b1 : 1'bz;  // Controlled_Buffer controlled_buffer_15
  assign CREGBUS[4] = wrGPR ? 1'b1 : 1'bz;  // Controlled_Buffer controlled_buffer_16
  assign CREGBUS[9] = ldDWL ? 1'b1 : 1'bz;  // Controlled_Buffer controlled_buffer_17
  assign CREGBUS[10] = ldDWH ? 1'b1 : 1'bz;  // Controlled_Buffer controlled_buffer_18
  assign CPSW[0] = clPSWSTART ? 1'b1 : 1'bz;  // Controlled_Buffer controlled_buffer_19
  assign CPSW[1] = ldI ? 1'b1 : 1'bz;  // Controlled_Buffer controlled_buffer_20
  assign CPSW[2] = ldV ? 1'b1 : 1'bz;  // Controlled_Buffer controlled_buffer_21
  assign CPSW[3] = ldN ? 1'b1 : 1'bz;  // Controlled_Buffer controlled_buffer_22
  assign CPSW[4] = ldZ ? 1'b1 : 1'bz;  // Controlled_Buffer controlled_buffer_23
  assign CPSW[5] = ldC ? 1'b1 : 1'bz;  // Controlled_Buffer controlled_buffer_24
  assign CPSW[6] = ldSTART ? 1'b1 : 1'bz;  // Controlled_Buffer controlled_buffer_25
  assign rdMEM = rdMEM_t ? 1'b1 : 1'bz;  // Controlled_Buffer controlled_buffer_26
  assign wrMEM = wrMEM_t ? 1'b1 : 1'bz;  // Controlled_Buffer controlled_buffer_27

  // Other names for the same wires on the sheet: A15__0[15:0] = A; immed = ADDRBUS[0]; regdir = ADDRBUS[4];
  //   ALU15__0[15:0] = ALU; B15__0[15:0] = B; CLK = in_2; FCBUS = in_3; HALT = INSTRUCBUS[0]; RTS = INSTRUCBUS[1];
  //   RTI = INSTRUCBUS[2]; INTE = INSTRUCBUS[3]; INTD = INSTRUCBUS[4]; ROL = INSTRUCBUS[5]; ROR = INSTRUCBUS[6];
  //   DEC = INSTRUCBUS[7]; BLEQ = INSTRUCBUS[8]; BNVF = INSTRUCBUS[9]; BLSSU = INSTRUCBUS[10]; BOVF = INSTRUCBUS[11];
  //   JEQL = INSTRUCBUS[12]; BR = INSTRUCBUS[13]; JMP = INSTRUCBUS[14]; JSR = INSTRUCBUS[15]; LD = INSTRUCBUS[16];
  //   ST = INSTRUCBUS[17]; SUB = INSTRUCBUS[18]; ADD = INSTRUCBUS[19]; MUL = INSTRUCBUS[20]; EXEC = PHASEFFBUS[2];
  //   PSWZ = PSW[1]; PSWN = PSW[2]; PSWV = PSW[3]; PSWC = PSW[4]; rst = in_1

  // Notes on the sheet:
  //   Operaciona jedinica
  //   Upravljacka jedinica
  //   Akumulator
  //   ALU
  //   Uslov za skok
endmodule

module INTR (
  input  in_1,
  input  in_2,
  input  in_3,
  input  [3:0] PHASEFFBUS,
  input  [15:0] PSW,
  input  [7:0] intr,
  input  [20:0] INSTRUCBUS,
  output [15:0] ADDIVTP,
  output [2:0] UEXT2__0,
  output inta,
  output [14:0] CMEMBUS,
  output [7:0] CFFBUS,
  output [11:0] CREGBUS,
  output rdMEM,
  output wrMEM
);

  wire and_2_out, and_3_out, and_4_out, brcnd, brnotFCBUS, brnotINTR, brnotprekid, bruncnd, clINTR, decSP,
       incMAR, ldDWH, ldDWL, ldMAR, ldMDR, ldPC, mxMAR0, mxMAR1, mxMAR2, mxMDR0, mxMDR1, mxMDR2, mxPC1,
       not_1_out, not_2_out, not_3_out, not_4_out, not_5_out, not_6_out, not_7_out, or_2_out, prekid, prper,
       rdMEM_t, stFETCH, wrMEM_t;
  wire [3:1] IVTDSP15__0;
  wire [4:0] reg5_inc_ld_1_a4__0, rom32x48_1_dout27__0;
  wire [15:0] IVTP15__0;
  wire [22:19] rom32x48_1_dout27__0_2;

  and and_1 (prekid, prper, PSW[15], not_2_out);
  not not_1 (not_1_out, in_1);
  REG5_INC_LD reg5_inc_ld_1 (
    .I4__0(rom32x48_1_dout27__0), .LD(or_2_out), .INC(not_4_out), .mr(not_1_out), .CLK(in_2),
    .A4__0(reg5_inc_ld_1_a4__0));
  DC3_8 dc3_8_1 (
    .En(1'b1), .X2__0(rom32x48_1_dout27__0_2[22:20]), .D1(bruncnd), .D2(brnotINTR), .D3(brnotprekid),
    .D4(brnotFCBUS));  // open: D0, D5, D6, D7
  not not_2 (not_2_out, INSTRUCBUS[0]);
  not not_3 (not_3_out, in_1);
  REG16_LD reg16_ld_1 (.CLK(in_2), .A15__0(IVTP15__0), .mr(not_3_out));  // open: I15__0, LD
  not not_4 (not_4_out, or_2_out);
  ROM32x48 rom32x48_1 (
    .A4__0(reg5_inc_ld_1_a4__0), .CS(1'b1),
    .DOUT27__0({rom32x48_1_dout27__0, rom32x48_1_dout27__0_2, ldMAR, ldMDR, decSP, mxMDR1, mxMDR0, mxMAR0, mxMAR1, wrMEM_t, mxMDR2, inta, mxMAR2, rdMEM_t, incMAR, ldDWH, ldDWL, ldPC, mxPC1, stFETCH, clINTR}));
  or or_1 (prper, intr[7], intr[6], intr[5], intr[4], intr[3], intr[2], intr[1], intr[0]);
  or or_2 (or_2_out, bruncnd, brcnd);
  CD8 cd8_1 (
    .En(1'b1), .C7(intr[7]), .C6(intr[6]), .C5(intr[5]), .C4(intr[4]), .C3(intr[3]), .C2(intr[2]),
    .C1(intr[1]), .C0(intr[0]), .Z2(UEXT2__0[2]), .Z1(UEXT2__0[1]), .Z0(UEXT2__0[0]));  // open: W
  REG3_LD_SL_SR reg3_ld_sl_sr_1 (
    .I2__0(UEXT2__0), .LD(inta), .CLK(in_2), .A2__0(IVTDSP15__0));  // open: IR, SR, IL, SL, mr
  ADD16 add16_1 (.C0(1'b0), .A(IVTP15__0), .B({{12{1'b0}}, IVTDSP15__0, 1'b0}), .F(ADDIVTP));  // open: C16
  not not_5 (not_5_out, PHASEFFBUS[3]);
  not not_6 (not_6_out, prekid);
  not not_7 (not_7_out, in_3);
  and and_2 (and_2_out, not_5_out, brnotINTR);
  and and_3 (and_3_out, not_6_out, brnotprekid);
  and and_4 (and_4_out, not_7_out, brnotFCBUS);
  or or_3 (brcnd, and_2_out, and_3_out, and_4_out);
  assign CMEMBUS[0] = ldMAR ? 1'b1 : 1'bz;  // Controlled_Buffer controlled_buffer_1
  assign CMEMBUS[1] = incMAR ? 1'b1 : 1'bz;  // Controlled_Buffer controlled_buffer_2
  assign CMEMBUS[2] = ldMDR ? 1'b1 : 1'bz;  // Controlled_Buffer controlled_buffer_3
  assign CMEMBUS[3] = ldPC ? 1'b1 : 1'bz;  // Controlled_Buffer controlled_buffer_4
  assign CMEMBUS[5] = mxMAR0 ? 1'b1 : 1'bz;  // Controlled_Buffer controlled_buffer_5
  assign CMEMBUS[6] = mxMAR1 ? 1'b1 : 1'bz;  // Controlled_Buffer controlled_buffer_6
  assign CMEMBUS[7] = mxMDR0 ? 1'b1 : 1'bz;  // Controlled_Buffer controlled_buffer_7
  assign CMEMBUS[8] = mxMDR1 ? 1'b1 : 1'bz;  // Controlled_Buffer controlled_buffer_8
  assign CMEMBUS[9] = mxMDR2 ? 1'b1 : 1'bz;  // Controlled_Buffer controlled_buffer_9
  assign CMEMBUS[11] = decSP ? 1'b1 : 1'bz;  // Controlled_Buffer controlled_buffer_10
  assign CMEMBUS[12] = mxPC1 ? 1'b1 : 1'bz;  // Controlled_Buffer controlled_buffer_11
  assign CMEMBUS[14] = mxMAR2 ? 1'b1 : 1'bz;  // Controlled_Buffer controlled_buffer_12
  assign CFFBUS[0] = stFETCH ? 1'b1 : 1'bz;  // Controlled_Buffer controlled_buffer_13
  assign CFFBUS[7] = clINTR ? 1'b1 : 1'bz;  // Controlled_Buffer controlled_buffer_14
  Controlled_Buffer controlled_buffer_15 (.in(1'b1), .en(inta));  // open: out
  assign CREGBUS[9] = ldDWL ? 1'b1 : 1'bz;  // Controlled_Buffer controlled_buffer_16
  assign CREGBUS[10] = ldDWH ? 1'b1 : 1'bz;  // Controlled_Buffer controlled_buffer_17
  assign rdMEM = rdMEM_t ? 1'b1 : 1'bz;  // Controlled_Buffer controlled_buffer_18
  assign wrMEM = wrMEM_t ? 1'b1 : 1'bz;  // Controlled_Buffer controlled_buffer_19

  // Other names for the same wires on the sheet: ldBR = inta; ADDIVTP15__0[15:0] = ADDIVTP; CLK = in_2; FCBUS = in_3;
  //   HALT = INSTRUCBUS[0]; intr7__0[7:0] = intr; INTR_t = PHASEFFBUS[3]; PSWI = PSW[15]; rst = in_1

  // Notes on the sheet:
  //   Operaciona jedinica
  //   Upravljacka jedinica
endmodule

module RAM (
  input  [15:0] in_1,
  input  in_2,
  input  [7:0] in_3,
  input  in_4,
  input  in_5,
  input  in_6,
  output [7:0] out_7,
  output out_8
);

  wire and_1_out, and_2_out, CNT0, LDCNT, not_1_out, not_2_out, not_3_out, notCNT0, or_1_out, rsff_2_q, sl,
       xor_1_out;
  wire [3:0] CNT, LFSR;

  RSFF rsff_1 (.S(in_6), .CLK(in_2), .R(1'b0), .Q(sl));  // open: Sd, Rd, notQ
  or or_1 (or_1_out, in_4, in_5);
  REG4_LD_SL_SR reg4_ld_sl_sr_1 (
    .I3__0(4'b1111), .LD(in_6), .IR(1'b0), .SR(1'b0), .IL(xor_1_out), .SL(sl), .CLK(in_2), .A3__0(LFSR));  // open: mr
  RisingEdge risingedge_1 (.INPUT(or_1_out), .CLK(in_2), .OUTPUT(LDCNT));
  MEM64Kx8 mem64kx8_1 (.WR_RD(in_4), .A15__0(in_1), .DIN(in_3), .CS(1'b1), .CLK(in_2), .DOUT(out_7));
  xor xor_1 (xor_1_out, LFSR[2], LFSR[3]);
  and and_1 (and_1_out, CNT0, not_1_out);
  not not_1 (not_1_out, LDCNT);
  RSFF rsff_2 (.S(LDCNT), .CLK(in_2), .R(and_1_out), .Rd(not_2_out), .Q(rsff_2_q));  // open: Sd, notQ
  not not_2 (not_2_out, in_6);
  and and_2 (and_2_out, rsff_2_q, CNT0);
  REG4m_DEC_LD reg4m_dec_ld_1 (
    .I3__0(LFSR), .LD(LDCNT), .Ein(notCNT0), .DEC(notCNT0), .CLK(in_2), .A3__0(CNT));  // open: Eout, mr
  or or_2 (notCNT0, CNT[0], CNT[1], CNT[2], CNT[3]);
  RSFF rsff_3 (.S(and_2_out), .CLK(in_2), .R(out_8), .Rd(not_3_out), .Q(out_8));  // open: Sd, notQ
  not not_3 (not_3_out, in_6);
  not not_4 (CNT0, notCNT0);

  // Other names for the same wires on the sheet: ADR[15:0] = in_1; CLK = in_2; DIN[7:0] = in_3; DOUT[7:0] = out_7;
  //   fc = out_8; RDMEM = in_5; rst = in_6; WRMEM = in_4

  // Notes on the sheet:
  //   Random broj predstavlja vreme pristupa memoriji
  //   Brojac za generisanje random broja 
  //   Jedinica za generisanje function complete (fc) signala
  //   Brojac za dekrementiranje random broja
endmodule
