// Logisim project ETFStudent.circ as structural Verilog: 15 circuits, main circuit REG32_LD
module REG32_LD (
  input  [31:0] I15__0,
  input  LD,
  input  mr,
  input  CLK,
  output [31:0] A15__0
);

  REG16_LD reg16_ld_1 (.I15__0(I15__0[31:16]), .LD(LD), .CLK(CLK), .A15__0(A15__0[31:16]), .mr(mr));
  REG16_LD reg16_ld_2 (.I15__0(I15__0[15:0]), .LD(LD), .CLK(CLK), .A15__0(A15__0[15:0]), .mr(mr));

  // Notes on the sheet:
  //   __
endmodule

module KMADR (
  input  immed,
  input  memdir,
  input  memind,
  input  regind,
  input  regdir,
  input  predec,
  input  preinc,
  output [4:0] Adr4__0
);

  assign Adr4__0 = immed ? 5'b00010 : 5'bz;  // Controlled_Buffer controlled_buffer_1
  assign Adr4__0 = memdir ? 5'b00011 : 5'bz;  // Controlled_Buffer controlled_buffer_2
  assign Adr4__0 = memind ? 5'b00100 : 5'bz;  // Controlled_Buffer controlled_buffer_3
  assign Adr4__0 = regind ? 5'b01010 : 5'bz;  // Controlled_Buffer controlled_buffer_4
  assign Adr4__0 = regdir ? 5'b01011 : 5'bz;  // Controlled_Buffer controlled_buffer_5
  assign Adr4__0 = predec ? 5'b01101 : 5'bz;  // Controlled_Buffer controlled_buffer_6
  assign Adr4__0 = preinc ? 5'b10001 : 5'bz;  // Controlled_Buffer controlled_buffer_7
endmodule

module KMOPR (
  input  HALT,
  input  RTS,
  input  RTI,
  input  INTE,
  input  INTD,
  input  ROL,
  input  ROR,
  input  DEC,
  input  BLEQ,
  input  BNVF,
  input  BLSSU,
  input  BOVF,
  input  JEQL,
  input  BR,
  input  JMP,
  input  JSR,
  input  LD,
  input  ST,
  input  SUB,
  input  ADD,
  input  MUL,
  output [5:0] Adr5__0
);

  assign Adr5__0 = HALT ? 6'b000010 : 6'bz;  // Controlled_Buffer controlled_buffer_1
  assign Adr5__0 = RTS ? 6'b000011 : 6'bz;  // Controlled_Buffer controlled_buffer_2
  assign Adr5__0 = RTI ? 6'b001010 : 6'bz;  // Controlled_Buffer controlled_buffer_3
  assign Adr5__0 = INTE ? 6'b010000 : 6'bz;  // Controlled_Buffer controlled_buffer_4
  assign Adr5__0 = INTD ? 6'b010001 : 6'bz;  // Controlled_Buffer controlled_buffer_5
  assign Adr5__0 = ROL ? 6'b010010 : 6'bz;  // Controlled_Buffer controlled_buffer_6
  assign Adr5__0 = ROR ? 6'b010100 : 6'bz;  // Controlled_Buffer controlled_buffer_7
  assign Adr5__0 = DEC ? 6'b010110 : 6'bz;  // Controlled_Buffer controlled_buffer_8
  assign Adr5__0 = BLEQ ? 6'b011000 : 6'bz;  // Controlled_Buffer controlled_buffer_9
  assign Adr5__0 = BNVF ? 6'b011010 : 6'bz;  // Controlled_Buffer controlled_buffer_10
  assign Adr5__0 = BLSSU ? 6'b011100 : 6'bz;  // Controlled_Buffer controlled_buffer_11
  assign Adr5__0 = BOVF ? 6'b011110 : 6'bz;  // Controlled_Buffer controlled_buffer_12
  assign Adr5__0 = JEQL ? 6'b100000 : 6'bz;  // Controlled_Buffer controlled_buffer_13
  assign Adr5__0 = JMP ? 6'b100011 : 6'bz;  // Controlled_Buffer controlled_buffer_14
  assign Adr5__0 = BR ? 6'b100010 : 6'bz;  // Controlled_Buffer controlled_buffer_15
  assign Adr5__0 = JSR ? 6'b100100 : 6'bz;  // Controlled_Buffer controlled_buffer_16
  assign Adr5__0 = LD ? 6'b101001 : 6'bz;  // Controlled_Buffer controlled_buffer_17
  assign Adr5__0 = ST ? 6'b101011 : 6'bz;  // Controlled_Buffer controlled_buffer_18
  assign Adr5__0 = SUB ? 6'b110010 : 6'bz;  // Controlled_Buffer controlled_buffer_19
  assign Adr5__0 = ADD ? 6'b110100 : 6'bz;  // Controlled_Buffer controlled_buffer_20
  assign Adr5__0 = MUL ? 6'b110110 : 6'bz;  // Controlled_Buffer controlled_buffer_21
endmodule

module REG6_INC_LD (
  input  [5:0] I5__0,
  input  LD,
  input  INC,
  input  mr,
  input  CLK,
  output [5:0] A5__0
);

  wire reg2m_inc_ld_2_cout, reg2m_inc_ld_3_cout;

  REG2m_INC_LD reg2m_inc_ld_1 (
    .I1__0(I5__0[5:4]), .LD(LD), .Cin(reg2m_inc_ld_2_cout), .INC(INC), .CLK(CLK), .A1__0(A5__0[5:4]), .mr(mr));  // open: Cout
  REG2m_INC_LD reg2m_inc_ld_2 (
    .I1__0(I5__0[3:2]), .LD(LD), .Cin(reg2m_inc_ld_3_cout), .INC(INC), .CLK(CLK), .Cout(reg2m_inc_ld_2_cout),
    .A1__0(A5__0[3:2]), .mr(mr));
  REG2m_INC_LD reg2m_inc_ld_3 (
    .I1__0(I5__0[1:0]), .LD(LD), .Cin(INC), .INC(INC), .CLK(CLK), .Cout(reg2m_inc_ld_3_cout),
    .A1__0(A5__0[1:0]), .mr(mr));

  // Notes on the sheet:
  //   __
endmodule

module ROM32x24 (
  input  [4:0] A4__0,
  input  CS,
  output [23:0] DOUT
);

  ROM #(.addrWidth(5), .dataWidth(24)) rom_1 (.addr(A4__0), .data(DOUT), .sel(CS));
endmodule

module GPR16x16 (
  input  [15:0] DI15__0,
  input  [3:0] A3__0,
  input  WR,
  input  CLK,
  output [15:0] DO15__0
);

  wire not_1_out;
  wire [15:0] gpr8x16_1_do15__0, gpr8x16_2_do15__0;

  GPR8x16 gpr8x16_1 (.DI15__0(DI15__0), .A2__0(A3__0[2:0]), .WR(WR), .CLK(CLK), .DO15__0(gpr8x16_1_do15__0));
  assign DO15__0 = A3__0[3] ? gpr8x16_1_do15__0 : 16'bz;  // Controlled_Buffer controlled_buffer_1
  GPR8x16 gpr8x16_2 (.DI15__0(DI15__0), .A2__0(A3__0[2:0]), .WR(WR), .CLK(CLK), .DO15__0(gpr8x16_2_do15__0));
  not not_1 (not_1_out, A3__0[3]);
  assign DO15__0 = not_1_out ? gpr8x16_2_do15__0 : 16'bz;  // Controlled_Buffer controlled_buffer_2

  // Other names for the same wires on the sheet: A2__0[2:0] = A3__0[2:0]; A3 = A3__0[3]; inREG[15:0] = DI15__0;
  //   outREG[15:0] = DO15__0
endmodule

module ALU16_ADD_SUB (
  input  Cin,
  input  [15:0] A,
  input  [15:0] B,
  input  add,
  input  sub,
  input  mul,
  output [15:0] F,
  output Cout
);

  wire adder_1_cout, subtractor_1_bout;
  wire [15:0] adder_1_out, multiplier_1_cout, multiplier_1_out, subtractor_1_out;

  Adder #(.width(16)) adder_1 (.a(A), .b(B), .out(adder_1_out), .cin(Cin), .cout(adder_1_cout));
  Subtractor #(.width(16)) subtractor_1 (.a(A), .b(B), .out(subtractor_1_out), .bin(Cin), .bout(subtractor_1_bout));
  Multiplier #(.width(16)) multiplier_1 (
    .a({{8{1'b0}}, A[7:0]}), .b({{8{1'b0}}, B[7:0]}), .out(multiplier_1_out), .cin({16{1'b0}}),
    .cout(multiplier_1_cout));
  assign F = add ? adder_1_out : 16'bz;  // Controlled_Buffer controlled_buffer_1
  assign Cout = add ? adder_1_cout : 1'bz;  // Controlled_Buffer controlled_buffer_2
  assign F = sub ? subtractor_1_out : 16'bz;  // Controlled_Buffer controlled_buffer_3
  assign Cout = sub ? subtractor_1_bout : 1'bz;  // Controlled_Buffer controlled_buffer_4
  assign F = mul ? multiplier_1_out : 16'bz;  // Controlled_Buffer controlled_buffer_5
  assign Cout = mul ? multiplier_1_cout[0] : 1'bz;  // Controlled_Buffer controlled_buffer_6
endmodule

module ROM64x46 (
  input  [5:0] A5__0,
  input  CS,
  output [31:0] DOUT31__0,
  output [15:0] DOUT47__32
);

  ROM #(.addrWidth(6), .dataWidth(16)) rom_1 (.addr(A5__0), .data(DOUT47__32), .sel(CS));
  ROM #(.addrWidth(6), .dataWidth(32)) rom_2 (.addr(A5__0), .data(DOUT31__0), .sel(CS));
endmodule

module REG16_LD_SR_SL (
  input  [15:0] I15__0,
  input  LD,
  input  IR,
  input  SR,
  input  IL,
  input  SL,
  input  mr,
  input  CLK,
  output [15:0] A15__0
);

  REG8_LD_SL_SR reg8_ld_sl_sr_1 (
    .I7__0(I15__0[15:8]), .LD(LD), .IR(IR), .SR(SR), .IL(A15__0[7]), .SL(SL), .CLK(CLK),
    .A7__0(A15__0[15:8]), .mr(mr));
  REG8_LD_SL_SR reg8_ld_sl_sr_2 (
    .I7__0(I15__0[7:0]), .LD(LD), .IR(A15__0[8]), .SR(SR), .IL(IL), .SL(SL), .CLK(CLK), .A7__0(A15__0[7:0]),
    .mr(mr));

  // Notes on the sheet:
  //   __
endmodule

module ROM32x48 (
  input  [4:0] A4__0,
  input  CS,
  output [27:0] DOUT27__0
);

  ROM #(.addrWidth(5), .dataWidth(28)) rom_1 (.addr(A4__0), .data(DOUT27__0), .sel(CS));
endmodule

module REG5_INC_LD (
  input  [4:0] I4__0,
  input  LD,
  input  INC,
  input  mr,
  input  CLK,
  output [4:0] A4__0
);

  wire reg1m_cl_inc_ld_1_cout, reg2m_inc_ld_2_cout;

  REG2m_INC_LD reg2m_inc_ld_1 (
    .I1__0(I4__0[4:3]), .LD(LD), .Cin(reg2m_inc_ld_2_cout), .INC(INC), .CLK(CLK), .A1__0(A4__0[4:3]), .mr(mr));  // open: Cout
  REG2m_INC_LD reg2m_inc_ld_2 (
    .I1__0(I4__0[2:1]), .LD(LD), .Cin(reg1m_cl_inc_ld_1_cout), .INC(INC), .CLK(CLK),
    .Cout(reg2m_inc_ld_2_cout), .A1__0(A4__0[2:1]), .mr(mr));
  REG1m_CL_INC_LD reg1m_cl_inc_ld_1 (
    .Ii(I4__0[0]), .LD(LD), .INC(INC), .Ci(INC), .CLK(CLK), .Ai(A4__0[0]), .Cout(reg1m_cl_inc_ld_1_cout),
    .mr(mr));  // open: CL

  // Notes on the sheet:
  //   __
endmodule

module ROM64x48 (
  input  [5:0] A5__0,
  input  CS,
  output [31:0] DOUT31__0,
  output [15:0] DOUT47__32
);

  ROM #(.addrWidth(6), .dataWidth(16)) rom_1 (.addr(A5__0), .data(DOUT47__32), .sel(CS));
  ROM #(.addrWidth(6), .dataWidth(32)) rom_2 (.addr(A5__0), .data(DOUT31__0), .sel(CS));
endmodule

module ROM32x24v2 (
  input  [4:0] A4__0,
  input  CS,
  output [23:0] DOUT
);

  ROM #(.addrWidth(5), .dataWidth(24)) rom_1 (.addr(A4__0), .data(DOUT), .sel(CS));
endmodule

module ROM64x52 (
  input  [5:0] A5__0,
  input  CS,
  output [31:0] DOUT31__0,
  output [19:0] DOUT51__32
);

  ROM #(.addrWidth(6), .dataWidth(20)) rom_1 (.addr(A5__0), .data(DOUT51__32), .sel(CS));
  ROM #(.addrWidth(6), .dataWidth(32)) rom_2 (.addr(A5__0), .data(DOUT31__0), .sel(CS));
endmodule

module ROM32x28 (
  input  [4:0] A4__0,
  input  CS,
  output [27:0] DOUT
);

  ROM #(.addrWidth(5), .dataWidth(28)) rom_1 (.addr(A4__0), .data(DOUT), .sel(CS));
endmodule
